// Logisim project taxi-meter.circ as structural Verilog: 10 circuits, main circuit main
module main (
  input  \启动 
);

  wire and_1_out, and_2_out, and_3_out, and_4_out, and_5_out, and_6_out, buffer_1_out, buffer_2_out,
       buffer_3_out, buffer_4_out, clock_1_out, clock_2_out, clock_3_out, clock_4_out, comparator_1_gt,
       comparator_1_lt, comparator_2_eq, comparator_2_gt, comparator_4_gt, comparator_4_lt, counter_1_carry,
       d_ff_1_qn, Km, Money, or_1_out, or_2_out, or_3_out, or_4_out, or_5_out, or_7_out, \乘客上下车 , \乘客在车上 ,
       \切换 , \切换Km , \毛刺_1_out , \清除上一位乘客数据 , \等待 , \等待In , \米计数器_carry , \行驶 , \行驶_等待 , \路程In ;
  wire [1:0] comparator_3_eq;
  wire [3:0] n9999_1_qa, n9999_1_qb, n9999_1_qc, n9999_1_qd, \个 , \分时显示 , \十 , \千 , \百 ;
  wire [4:0] \剩余m数 ;
  wire [7:0] \剩余s数 ;
  wire [13:0] adder_1_out, bit_extender_1_out, bit_extender_2_out, bit_extender_3_out, \Km价格 , \Km数 ,
       multiplier_1_out, \不足1min , \公里计费器_1_money , \分钟钱 , \剩余 , \总价格 ;

  // Probe on \分钟钱 
  LED led_1 (.in(\行驶 ));
  LED led_2 (.in(\等待 ));
  LED led_3 (.in(\乘客在车上 ));
  // Probe on \Km数 
  // Probe on \Km价格 
  \公里计费器  \u_公里计费器_1  (.Km(\Km数 ), .Money(\公里计费器_1_money ));
  Adder #(.width(14)) adder_1 (.a(\分钟钱 ), .b(\不足1min ), .out(adder_1_out));  // open: cin, cout
  Comparator #(.width(5)) comparator_1 (
    .a(\剩余m数 ), .b(5'b00001), .gt(comparator_1_gt), .lt(comparator_1_lt));  // open: eq
  Hex_Digit_Display hex_digit_display_1 (.value(\百 ));  // open: dp
  Hex_Digit_Display hex_digit_display_2 (.value(\千 ));  // open: dp
  // Probe on \总价格 
  Button \u_上下车切换  (.out(\乘客上下车 ));
  Button reset (.out(\清除上一位乘客数据 ));
  Adder #(.width(14)) adder_2 (.a(\公里计费器_1_money ), .b(\剩余 ), .out(\Km价格 ));  // open: cin, cout
  or or_1 (or_1_out, comparator_1_gt, comparator_1_lt);
  assign bit_extender_1_out = {{13{1'b0}}, or_1_out};  // Bit_Extender bit_extender_1
  Comparator #(.width(14)) comparator_2 (.a(\Km数 ), .b(14'h3), .gt(comparator_2_gt), .eq(comparator_2_eq));  // open: lt
  Hex_Digit_Display hex_digit_display_3 (.value(\十 ));  // open: dp
  Hex_Digit_Display hex_digit_display_4 (.value(\个 ));  // open: dp
  Hex_Digit_Display hex_digit_display_5 (.value(\分时显示 ), .dp(clock_1_out));
  Clock clock_1 (.out(clock_1_out));
  Button \u_模拟路程输入  (.out(\路程In ));
  Adder #(.width(14)) adder_3 (.a(\Km价格 ), .b(adder_1_out), .out(\总价格 ));  // open: cin, cout
  or or_2 (or_2_out, comparator_2_gt, comparator_2_eq);
  LED \u_显示Km  (.in(\切换Km ));
  LED \u_显示Km_2  (.in(Km));
  LED \u_显示Money  (.in(Money));
  Button \u_行等切换  (.out(\行驶_等待 ));
  Button \u_模拟等待输入  (.out(\等待In ));
  Clock clock_2 (.out(clock_2_out));
  \分时显示  \u_分时显示_1  (
    .\重置 (or_3_out), .\分时CLK (clock_2_out), .\显示Km (Km), .\Km数 (\Km数 ), .\显示Money (Money), .\金额 (\总价格 ),
    .\分时输出 (\分时显示 ));
  \切换显示  \u_切换显示_1  (
    .\显示Km (\切换Km ), .\分时CLK (\乘客在车上 ), .\Km数 (\Km数 ), .\显示Money (\切换 ), .\使能 (\启动 ), .\个 (\个 ), .\十 (\十 ),
    .\金额 (\总价格 ), .\百 (\百 ), .\千 (\千 ));
  Multiplier #(.width(14)) multiplier_1 (.a(bit_extender_1_out), .b(14'h3), .out(multiplier_1_out));  // open: cin, cout
  LED \u_显示Money_2  (.in(\切换 ));
  or or_3 (or_3_out, \乘客上下车 , \毛刺_1_out );
  Multiplexer #(.width(14), .enable("false")) multiplexer_1 (
    .in0({14{1'b0}}), .in1(multiplier_1_out), .out(\剩余 ), .sel(or_2_out));
  \毛刺  \u_毛刺_1  (.IN(\启动 ), .OUT(\毛刺_1_out ));
  or or_4 (or_4_out, and_1_out, buffer_1_out);
  and and_1 (and_1_out, clock_3_out, ~\路程In );  // AND_Gate
  Clock clock_3 (.out(clock_3_out));
  Clock clock_4 (.out(clock_4_out));
  Counter #(.width(5), .max('h14)) \u_米计数器  (
    .Q(\剩余m数 ), .carry(\米计数器_carry ), .clk(and_2_out), .clr(\清除上一位乘客数据 ));  // open: load, D, count
  and and_2 (and_2_out, or_4_out, \行驶 , \乘客在车上 );
  buf buffer_1 (buffer_1_out, buffer_2_out);
  buf buffer_2 (buffer_2_out, \路程In );
  and and_3 (and_3_out, clock_4_out, ~\等待In );  // AND_Gate
  or or_5 (or_5_out, and_3_out, buffer_4_out);
  buf buffer_3 (buffer_3_out, \等待In );
  buf buffer_4 (buffer_4_out, buffer_3_out);
  Comparator comparator_3 (.a(\剩余s数 ), .b(8'h3b), .eq(comparator_3_eq[0]));  // open: gt, lt
  Comparator comparator_4 (.a(\剩余s数 ), .b({8{1'b0}}), .gt(comparator_4_gt), .lt(comparator_4_lt));  // open: eq
  or or_6 (comparator_3_eq[1], comparator_4_gt, comparator_4_lt);
  // Probe on n9999_1_qd
  _9999 u_9999_1 (
    .CTt(1'b1), .CTp(1'b1), .QC(n9999_1_qc), .QD(n9999_1_qd), .QB(n9999_1_qb), .QA(n9999_1_qa),
    .CLK(\米计数器_carry ), .RES(\清除上一位乘客数据 ), .LDn(1'b1), .CRn(\清除上一位乘客数据 ));  // open: DD, DB, DA, DC, CO
  and and_4 (and_4_out, \启动 , \乘客上下车 );
  and and_5 (and_5_out, \行驶_等待 , \启动 );
  Counter #(.max('h3b)) counter_1 (
    .Q(\剩余s数 ), .carry(counter_1_carry), .clk(and_6_out), .clr(\清除上一位乘客数据 ));  // open: load, D, count
  and and_6 (and_6_out, \等待 , or_5_out, \乘客在车上 );
  assign bit_extender_2_out = {{13{1'b0}}, 1'b1};  // Bit_Extender bit_extender_2
  assign bit_extender_3_out = {{13{1'b0}}, 1'b0};  // Bit_Extender bit_extender_3
  // Probe on n9999_1_qc
  // Probe on n9999_1_qa
  // Probe on n9999_1_qb
  \转2进制  \u_转2进制_1  (
    .\进位 (or_7_out), .\个位 (n9999_1_qa), .\十位 (n9999_1_qb), .\百位 (n9999_1_qc), .\千位 (n9999_1_qd), .out(\Km数 ));
  D_Flip_Flop d_ff_1 (.clk(and_4_out), .D(d_ff_1_qn), .Q(\乘客在车上 ), .Qn(d_ff_1_qn));  // open: preset, en, reset
  D_Flip_Flop d_ff_2 (.clk(and_5_out), .D(\等待 ), .Q(\行驶 ), .Qn(\等待 ));  // open: preset, en, reset
  Counter #(.width(14), .max('h3fff)) counter_2 (
    .Q(\分钟钱 ), .clk(counter_1_carry), .clr(\清除上一位乘客数据 ));  // open: load, D, count, carry
  Multiplexer #(.select(2), .width(14), .enable("false")) multiplexer_2 (
    .in0(bit_extender_3_out), .in1(bit_extender_3_out), .in2(bit_extender_2_out), .in3(bit_extender_3_out),
    .out(\不足1min ), .sel(comparator_3_eq));
  or or_7 (or_7_out, \剩余m数 [4], \剩余m数 [3], \剩余m数 [2], \剩余m数 [1], \剩余m数 [0]);

  // Other names for the same wires on the sheet: Start = \启动 ; 等待时间[13:0] = \分钟钱 

  // Notes on the sheet:
  //   启动: pull=down
  //   主控模块
  //   A
  //   指示灯
  //   Debug显示
  //   计费模块
  //   显示模块
  //   B
  //   C
  //   里程模块
  //   等待模块
  //   10：有剩余时间+1
  //   11：要进位了，价格不+1
endmodule

module _74Ls160 (
  input  D0,
  input  D1,
  input  D2,
  input  D3,
  input  CTt,
  input  CTp,
  input  LDn,
  input  CRn,
  input  CLK,
  output Q0,
  output Q1,
  output Q2,
  output Q3,
  output CO
);

  wire and_1_out, buffer_2_out, counter_1_carry, not_1_out, not_2_out;
  wire [3:0] counter_1_q;

  and and_1 (and_1_out, CTt, CTp);
  not not_1 (not_1_out, LDn);
  assign {Q3, Q2, Q1, Q0} = counter_1_q;  // Buffer buffer_1, 4 bits wide
  Counter #(.width(4), .max('h9), .trigger("falling")) counter_1 (
    .load(not_1_out), .D({D3, D2, D1, D0}), .count(and_1_out), .Q(counter_1_q), .carry(counter_1_carry),
    .clk(CLK), .clr(not_2_out));
  not not_2 (not_2_out, CRn);
  buf buffer_2 (buffer_2_out, counter_1_carry);
  and and_2 (CO, counter_1_carry, buffer_2_out, CTt);

  // Notes on the sheet:
  //   数据输入端
  //   计数使能端
  //   同步预制端
  //   异步清零端
  //   计数器输出端
  //   进位输出端
endmodule

// Km计数器
module \_99计数器  (
  input  [3:0] DB,
  input  [3:0] DA,
  input  CTt,
  input  CTp,
  input  CLK,
  input  RES,
  input  LDn,
  input  CRn,
  output [3:0] QA,
  output [3:0] QB,
  output CO
);

  wire n74ls160_1_co, n74ls160_2_co, not_1_out, or_1_out, or_2_out;

  or or_1 (or_1_out, CLK, RES);
  _74Ls160 u_74ls160_1 (
    .D0(DA[0]), .D1(DA[1]), .D2(DA[2]), .D3(DA[3]), .CTt(CTt), .CTp(CTp), .LDn(LDn), .CRn(not_1_out),
    .CLK(or_1_out), .Q0(QA[0]), .Q1(QA[1]), .Q2(QA[2]), .Q3(QA[3]), .CO(n74ls160_1_co));
  or or_2 (or_2_out, n74ls160_1_co, RES);
  not not_1 (not_1_out, CRn);
  _74Ls160 u_74ls160_2 (
    .D0(DB[0]), .D1(DB[1]), .D2(DB[2]), .D3(DB[3]), .CTt(CTt), .CTp(CTp), .LDn(LDn), .CRn(not_1_out),
    .CLK(or_2_out), .Q0(QB[0]), .Q1(QB[1]), .Q2(QB[2]), .Q3(QB[3]), .CO(n74ls160_2_co));
  and and_1 (CO, n74ls160_2_co, or_2_out);

  // Notes on the sheet:
  //   低位
  //   高位
endmodule

module \转2进制  (
  input  \进位 ,
  input  [3:0] \个位 ,
  input  [3:0] \十位 ,
  input  [3:0] \百位 ,
  input  [3:0] \千位 ,
  output [13:0] out
);

  wire [3:0] multiplier_1_cout, multiplier_1_out, multiplier_2_cout, multiplier_2_out, multiplier_3_cout,
       multiplier_3_out;
  wire [7:0] adder_1_out;
  wire [9:0] multiplier_4_cout, multiplier_4_out, multiplier_5_cout, multiplier_5_out;
  wire [19:0] adder_2_out, bit_extender_1_out, multiplier_6_out;
  wire [19:14] adder_3_out;

  Multiplier #(.width(4)) multiplier_1 (
    .a(\十位 ), .b(4'b1010), .out(multiplier_1_out), .cout(multiplier_1_cout));  // open: cin
  Multiplier #(.width(4)) multiplier_2 (
    .a(\百位 ), .b(4'b1010), .out(multiplier_2_out), .cout(multiplier_2_cout));  // open: cin
  Multiplier #(.width(4)) multiplier_3 (
    .a(\千位 ), .b(4'b1010), .out(multiplier_3_out), .cout(multiplier_3_cout));  // open: cin
  Adder adder_1 (
    .a({4'b0000, \个位 }), .b({multiplier_1_cout, multiplier_1_out}), .out(adder_1_out), .cin(\进位 ));  // open: cout
  Multiplier #(.width(10)) multiplier_4 (
    .a({2'b00, multiplier_2_cout, multiplier_2_out}), .b(10'ha), .out(multiplier_4_out),
    .cout(multiplier_4_cout));  // open: cin
  Multiplier #(.width(10)) multiplier_5 (
    .a({2'b00, multiplier_3_cout, multiplier_3_out}), .b(10'ha), .out(multiplier_5_out),
    .cout(multiplier_5_cout));  // open: cin
  assign bit_extender_1_out = {{12{1'b0}}, adder_1_out};  // Bit_Extender bit_extender_1
  Multiplier #(.width(20)) multiplier_6 (
    .a({multiplier_5_cout, multiplier_5_out}), .b(20'ha), .out(multiplier_6_out));  // open: cin, cout
  Adder #(.width(20)) adder_2 (
    .a(bit_extender_1_out), .b({multiplier_4_cout, multiplier_4_out}), .out(adder_2_out));  // open: cin, cout
  Adder #(.width(20)) adder_3 (.a(adder_2_out), .b(multiplier_6_out), .out({adder_3_out, out}));  // open: cin, cout
endmodule

module \公里计费器  (
  input  [13:0] Km,
  output [13:0] Money
);

  wire buffer_1_out, comparator_1_gt, not_1_out;
  wire [13:0] multiplier_1_cout, multiplier_1_out, subtractor_1_out;
  wire [27:0] adder_1_out, controlled_buffer_1_out;

  Subtractor #(.width(14)) subtractor_1 (.a(Km), .b(14'h3), .out(subtractor_1_out));  // open: bin, bout
  Comparator #(.width(14)) comparator_1 (.a(Km), .b(14'h3), .gt(comparator_1_gt));  // open: eq, lt
  Multiplier #(.width(14)) multiplier_1 (
    .a(subtractor_1_out), .b(14'h3), .out(multiplier_1_out), .cout(multiplier_1_cout));  // open: cin
  not not_1 (not_1_out, comparator_1_gt);
  assign controlled_buffer_1_out = not_1_out ? 28'ha : 28'bz;  // Controlled_Buffer controlled_buffer_1
  Adder #(.width(28)) adder_1 (
    .a({multiplier_1_cout, multiplier_1_out}), .b(28'ha), .out(adder_1_out));  // open: cin, cout
  assign controlled_buffer_1_out = buffer_1_out ? adder_1_out : 28'bz;  // Controlled_Buffer controlled_buffer_2
  buf buffer_1 (buffer_1_out, comparator_1_gt);
  Bit_Extender #(.in_width(28), .out_width(14)) bit_extender_1 (.in(controlled_buffer_1_out), .out(Money));
  // Probe on controlled_buffer_1_out

  // Notes on the sheet:
  //   十进制：10（起步价）
endmodule

module \切换显示  (
  input  \分时CLK ,
  input  [13:0] \Km数 ,
  input  \使能 ,
  input  [13:0] \金额 ,
  output \显示Km ,
  output \显示Money ,
  output [3:0] \个 ,
  output [3:0] \十 ,
  output [3:0] \百 ,
  output [3:0] \千 
);

  wire buffer_1_out, buffer_2_out, buffer_3_out, buffer_4_out, not_1_out, not_2_out, not_3_out, not_4_out,
       not_5_out;
  wire [3:0] controlled_buffer_1_out, controlled_buffer_4_out, controlled_buffer_7_out,
       controlled_buffer_10_out;
  wire [13:0] divider_1_out, divider_1_rem, divider_2_out, divider_2_rem, divider_3_out, divider_3_rem,
       divider_4_out, divider_4_rem, divider_5_out, divider_5_rem, divider_6_out, divider_6_rem;

  Divider #(.width(14)) divider_1 (.a(\Km数 ), .b(14'h3e8), .out(divider_1_out), .rem(divider_1_rem));  // open: upper
  Divider #(.width(14)) divider_2 (.a(\金额 ), .b(14'h3e8), .out(divider_2_out), .rem(divider_2_rem));  // open: upper
  Divider #(.width(14)) divider_3 (
    .a(divider_1_rem), .b(14'h64), .out(divider_3_out), .rem(divider_3_rem));  // open: upper
  Divider #(.width(14)) divider_4 (
    .a(divider_3_rem), .b(14'ha), .out(divider_4_out), .rem(divider_4_rem));  // open: upper
  Divider #(.width(14)) divider_5 (
    .a(divider_2_rem), .b(14'h64), .out(divider_5_out), .rem(divider_5_rem));  // open: upper
  Divider #(.width(14)) divider_6 (
    .a(divider_5_rem), .b(14'ha), .out(divider_6_out), .rem(divider_6_rem));  // open: upper
  not not_1 (not_1_out, \分时CLK );
  buf buffer_1 (buffer_1_out, \分时CLK );
  not not_2 (not_2_out, \分时CLK );
  buf buffer_2 (buffer_2_out, \分时CLK );
  not not_3 (not_3_out, \分时CLK );
  buf buffer_3 (buffer_3_out, \分时CLK );
  not not_4 (not_4_out, \分时CLK );
  buf buffer_4 (buffer_4_out, \分时CLK );
  not not_5 (not_5_out, \分时CLK );
  assign controlled_buffer_1_out = not_1_out ? divider_6_rem[3:0] : 4'bz;  // Controlled_Buffer controlled_buffer_1
  assign \个  = \使能  ? controlled_buffer_1_out : 4'bz;  // Controlled_Buffer controlled_buffer_2
  assign controlled_buffer_1_out = buffer_1_out ? divider_4_rem[3:0] : 4'bz;  // Controlled_Buffer controlled_buffer_3
  assign controlled_buffer_4_out = not_2_out ? divider_6_out[3:0] : 4'bz;  // Controlled_Buffer controlled_buffer_4
  assign \十  = \使能  ? controlled_buffer_4_out : 4'bz;  // Controlled_Buffer controlled_buffer_5
  assign controlled_buffer_4_out = buffer_2_out ? divider_4_out[3:0] : 4'bz;  // Controlled_Buffer controlled_buffer_6
  assign controlled_buffer_7_out = not_3_out ? divider_5_out[3:0] : 4'bz;  // Controlled_Buffer controlled_buffer_7
  assign \百  = \使能  ? controlled_buffer_7_out : 4'bz;  // Controlled_Buffer controlled_buffer_8
  assign controlled_buffer_7_out = buffer_3_out ? divider_3_out[3:0] : 4'bz;  // Controlled_Buffer controlled_buffer_9
  assign controlled_buffer_10_out = not_4_out ? divider_2_out[3:0] : 4'bz;  // Controlled_Buffer controlled_buffer_10
  assign \千  = \使能  ? controlled_buffer_10_out : 4'bz;  // Controlled_Buffer controlled_buffer_11
  assign controlled_buffer_10_out = buffer_4_out ? divider_1_out[3:0] : 4'bz;  // Controlled_Buffer controlled_buffer_12
  and and_1 (\显示Km , \分时CLK , \使能 );
  and and_2 (\显示Money , not_5_out, \使能 );
  Pull_Resistor pull_resistor_1 (.node(\个 ));
  Pull_Resistor pull_resistor_2 (.node(\十 ));
  Pull_Resistor pull_resistor_3 (.node(\百 ));
  Pull_Resistor pull_resistor_4 (.node(\千 ));

  // Notes on the sheet:
  //   十进制：100
  //   十进制：10
  //   十进制：100
  //   十进制：10
  //   百位
  //   十位
  //   个位
  //   百位
  //   十位
  //   个位
endmodule

module \分时显示  (
  input  \重置 ,
  input  \分时CLK ,
  input  [13:0] \Km数 ,
  input  [13:0] \金额 ,
  output \显示Km ,
  output \显示Money ,
  output [3:0] \分时输出 
);

  wire and_1_out, buffer_1_out, buffer_2_out, or_1_out, shift_register_1_out, shift_register_1_q0,
       shift_register_1_q1, shift_register_1_q2, shift_register_1_q3, shift_register_1_q4,
       shift_register_1_q5, shift_register_1_q6, shift_register_1_q7, shift_register_1_q8;
  wire [13:0] divider_1_out, divider_1_rem, divider_2_out, divider_2_rem, divider_3_out, divider_3_rem,
       divider_4_out, divider_4_rem, divider_5_out, divider_5_rem, divider_6_out, divider_6_rem;

  Divider #(.width(14)) divider_1 (.a(\Km数 ), .b(14'h3e8), .out(divider_1_out), .rem(divider_1_rem));  // open: upper
  Divider #(.width(14)) divider_2 (.a(\金额 ), .b(14'h3e8), .out(divider_2_out), .rem(divider_2_rem));  // open: upper
  Divider #(.width(14)) divider_3 (
    .a(divider_1_rem), .b(14'h64), .out(divider_3_out), .rem(divider_3_rem));  // open: upper
  Divider #(.width(14)) divider_4 (
    .a(divider_2_rem), .b(14'h64), .out(divider_4_out), .rem(divider_4_rem));  // open: upper
  buf buffer_1 (buffer_1_out, \重置 );
  buf buffer_2 (buffer_2_out, buffer_1_out);
  and and_1 (and_1_out, ~\重置 , \分时CLK );  // AND_Gate
  Divider #(.width(14)) divider_5 (
    .a(divider_3_rem), .b(14'ha), .out(divider_5_out), .rem(divider_5_rem));  // open: upper
  Divider #(.width(14)) divider_6 (
    .a(divider_4_rem), .b(14'ha), .out(divider_6_out), .rem(divider_6_rem));  // open: upper
  Shift_Register #(.length(10)) shift_register_1 (
    .in(shift_register_1_out), .clk(or_1_out), .out(shift_register_1_out), .load(buffer_1_out), .d0(1'b1),
    .q0(shift_register_1_q0), .d1(1'b0), .q1(shift_register_1_q1), .d2(1'b0), .q2(shift_register_1_q2),
    .d3(1'b0), .q3(shift_register_1_q3), .d4(1'b0), .q4(shift_register_1_q4), .d5(1'b0),
    .q5(shift_register_1_q5), .d6(1'b0), .q6(shift_register_1_q6), .d7(1'b0), .q7(shift_register_1_q7),
    .d8(1'b0), .q8(shift_register_1_q8), .d9(1'b0));  // open: shift, clr, q9
  or or_1 (or_1_out, buffer_2_out, and_1_out);
  assign \分时输出  = shift_register_1_q1 ? divider_3_out[3:0] : 4'bz;  // Controlled_Buffer controlled_buffer_1
  assign \分时输出  = shift_register_1_q0 ? divider_1_out[3:0] : 4'bz;  // Controlled_Buffer controlled_buffer_2
  assign \分时输出  = shift_register_1_q2 ? divider_5_out[3:0] : 4'bz;  // Controlled_Buffer controlled_buffer_3
  assign \分时输出  = shift_register_1_q3 ? divider_5_rem[3:0] : 4'bz;  // Controlled_Buffer controlled_buffer_4
  assign \分时输出  = shift_register_1_q6 ? divider_4_out[3:0] : 4'bz;  // Controlled_Buffer controlled_buffer_5
  assign \分时输出  = shift_register_1_q4 ? divider_2_out[3:0] : 4'bz;  // Controlled_Buffer controlled_buffer_6
  or or_2 (\显示Km , shift_register_1_q1, shift_register_1_q0, shift_register_1_q3, shift_register_1_q2);
  assign \分时输出  = shift_register_1_q7 ? divider_6_out[3:0] : 4'bz;  // Controlled_Buffer controlled_buffer_7
  assign \分时输出  = shift_register_1_q5 ? 4'b0000 : 4'bz;  // Controlled_Buffer controlled_buffer_8
  assign \分时输出  = shift_register_1_q8 ? divider_6_rem[3:0] : 4'bz;  // Controlled_Buffer controlled_buffer_9
  or or_3 (\显示Money , shift_register_1_q5, shift_register_1_q6, shift_register_1_q7, shift_register_1_q8);

  // Notes on the sheet:
  //   百位
  //   十位
  //   个位
  //   百位
  //   十位
  //   个位
endmodule

module \毛刺  (
  input  IN,
  output OUT
);

  wire buffer_1_out, t_ff_1_q, xor_1_out;

  xor xor_1 (xor_1_out, IN, t_ff_1_q);
  buf buffer_1 (buffer_1_out, IN);
  T_Flip_Flop t_ff_1 (.clk(OUT), .T(xor_1_out), .Q(t_ff_1_q), .preset(1'b0), .reset(1'b0), .en(1'b1));  // open: Qn
  xor xor_2 (OUT, buffer_1_out, t_ff_1_q);
endmodule

module _999 (
  input  [3:0] DB,
  input  [3:0] DA,
  input  [3:0] DC,
  input  CTt,
  input  CTp,
  input  CLK,
  input  RES,
  input  LDn,
  input  CRn,
  output [3:0] QC,
  output [3:0] QB,
  output [3:0] QA,
  output CO
);

  wire n74ls160_1_co, n74ls160_2_co, n74ls160_3_co, not_1_out, or_1_out, or_2_out, or_3_out;

  or or_1 (or_1_out, CLK, RES);
  _74Ls160 u_74ls160_1 (
    .D0(DA[0]), .D1(DA[1]), .D2(DA[2]), .D3(DA[3]), .CTt(CTt), .CTp(CTp), .LDn(LDn), .CRn(not_1_out),
    .CLK(or_1_out), .Q0(QA[0]), .Q1(QA[1]), .Q2(QA[2]), .Q3(QA[3]), .CO(n74ls160_1_co));
  or or_2 (or_2_out, n74ls160_1_co, RES);
  not not_1 (not_1_out, CRn);
  _74Ls160 u_74ls160_2 (
    .D0(DB[0]), .D1(DB[1]), .D2(DB[2]), .D3(DB[3]), .CTt(CTt), .CTp(CTp), .LDn(LDn), .CRn(not_1_out),
    .CLK(or_2_out), .Q0(QB[0]), .Q1(QB[1]), .Q2(QB[2]), .Q3(QB[3]), .CO(n74ls160_2_co));
  or or_3 (or_3_out, n74ls160_2_co, RES);
  _74Ls160 u_74ls160_3 (
    .D0(DC[0]), .D1(DC[1]), .D2(DC[2]), .D3(DC[3]), .CTt(CTt), .CTp(CTp), .LDn(LDn), .CRn(not_1_out),
    .CLK(or_3_out), .Q0(QC[0]), .Q1(QC[1]), .Q2(QC[2]), .Q3(QC[3]), .CO(n74ls160_3_co));
  and and_1 (CO, n74ls160_3_co, or_3_out);

  // Notes on the sheet:
  //   低位
  //   高位
endmodule

module _9999 (
  input  [3:0] DD,
  input  [3:0] DB,
  input  [3:0] DA,
  input  [3:0] DC,
  input  CTt,
  input  CTp,
  input  CLK,
  input  RES,
  input  LDn,
  input  CRn,
  output [3:0] QC,
  output [3:0] QD,
  output [3:0] QB,
  output [3:0] QA,
  output CO
);

  wire n74ls160_1_co, n74ls160_2_co, n74ls160_3_co, n74ls160_4_co, not_1_out, or_1_out, or_2_out, or_3_out,
       or_4_out;

  or or_1 (or_1_out, CLK, RES);
  _74Ls160 u_74ls160_1 (
    .D0(DA[0]), .D1(DA[1]), .D2(DA[2]), .D3(DA[3]), .CTt(CTt), .CTp(CTp), .LDn(LDn), .CRn(not_1_out),
    .CLK(or_1_out), .Q0(QA[0]), .Q1(QA[1]), .Q2(QA[2]), .Q3(QA[3]), .CO(n74ls160_1_co));
  not not_1 (not_1_out, CRn);
  or or_2 (or_2_out, n74ls160_1_co, RES);
  _74Ls160 u_74ls160_2 (
    .D0(DB[0]), .D1(DB[1]), .D2(DB[2]), .D3(DB[3]), .CTt(CTt), .CTp(CTp), .LDn(LDn), .CRn(not_1_out),
    .CLK(or_2_out), .Q0(QB[0]), .Q1(QB[1]), .Q2(QB[2]), .Q3(QB[3]), .CO(n74ls160_2_co));
  or or_3 (or_3_out, n74ls160_2_co, RES);
  _74Ls160 u_74ls160_3 (
    .D0(DC[0]), .D1(DC[1]), .D2(DC[2]), .D3(DC[3]), .CTt(CTt), .CTp(CTp), .LDn(LDn), .CRn(not_1_out),
    .CLK(or_3_out), .Q0(QC[0]), .Q1(QC[1]), .Q2(QC[2]), .Q3(QC[3]), .CO(n74ls160_3_co));
  or or_4 (or_4_out, n74ls160_3_co, RES);
  _74Ls160 u_74ls160_4 (
    .D0(DD[0]), .D1(DD[1]), .D2(DD[2]), .D3(DD[3]), .CTt(CTt), .CTp(CTp), .LDn(LDn), .CRn(not_1_out),
    .CLK(or_4_out), .Q0(QD[0]), .Q1(QD[1]), .Q2(QD[2]), .Q3(QD[3]), .CO(n74ls160_4_co));
  and and_1 (CO, n74ls160_4_co, or_4_out);

  // Notes on the sheet:
  //   低位
  //   高位
endmodule
